# Fritzing sketch data (saved by Fritzing 0.9.4)

parts:
  Raspberry_Pi_1 = Raspberry Pi 3 [part_number=RPI-3-V1.2]
  Part1 = Arduino Mega 2560 (Rev3)
  Air_quality_(SDS1) = SDS011 - dust sensor [part_number=1]
  Smoke_detector_(FC22) = MQ-7 breakout
  Raspberry_Pi_Sense_Hat1 = Raspberry Pi Sense Hat
  USBTTL1 = USB A Plug  # not connected

nets:
  3V3: Raspberry_Pi_1.3v3, Raspberry_Pi_1.3V3, Raspberry_Pi_Sense_Hat1.3v3, Raspberry_Pi_Sense_Hat1.3V3
  N1: Raspberry_Pi_1.GPIO2, Raspberry_Pi_Sense_Hat1.GPIO2
  N2: Raspberry_Pi_1.GPIO3, Raspberry_Pi_Sense_Hat1.GPIO3
  N3: Raspberry_Pi_1.GPIO4, Raspberry_Pi_Sense_Hat1.GIPO4
  GND: Raspberry_Pi_1.GND, Raspberry_Pi_Sense_Hat1.GND
  N4: Raspberry_Pi_1.GPIO17, Raspberry_Pi_Sense_Hat1.GIPO17
  N5: Raspberry_Pi_1.GPIO27, Raspberry_Pi_Sense_Hat1.GIPO27
  N6: Raspberry_Pi_1.GPIO22, Raspberry_Pi_Sense_Hat1.GIPO22
  N7: Raspberry_Pi_1.GPIO10, Raspberry_Pi_Sense_Hat1.GIPO10
  N8: Raspberry_Pi_1.GPIO9, Raspberry_Pi_Sense_Hat1.GIPO9
  N9: Raspberry_Pi_1.GPIO11, Raspberry_Pi_Sense_Hat1.GIPO11
  N10: Raspberry_Pi_1.ID_SD, Raspberry_Pi_Sense_Hat1.ID_SD
  N11: Raspberry_Pi_1.GPIO5, Raspberry_Pi_Sense_Hat1.GIPO5
  N12: Raspberry_Pi_1.GPIO6, Raspberry_Pi_Sense_Hat1.GIPO6
  N13: Raspberry_Pi_1.GPIO13, Raspberry_Pi_Sense_Hat1.GIPO13
  N14: Raspberry_Pi_1.GPIO19, Raspberry_Pi_Sense_Hat1.GIPO19
  N15: Raspberry_Pi_1.GPIO26, Raspberry_Pi_Sense_Hat1.GIPO26
  N16: Raspberry_Pi_1.GPIO21, Raspberry_Pi_Sense_Hat1.GIPO21
  N17: Raspberry_Pi_1.GPIO20, Raspberry_Pi_Sense_Hat1.GIPO20
  N18: Raspberry_Pi_1.GPIO16, Raspberry_Pi_Sense_Hat1.GIPO16
  N19: Raspberry_Pi_1.GPIO12, Raspberry_Pi_Sense_Hat1.GIPO12
  N20: Raspberry_Pi_1.ID_SC, Raspberry_Pi_Sense_Hat1.ID_SC
  N21: Raspberry_Pi_1.GPIO7, Raspberry_Pi_Sense_Hat1.GIPO7
  N22: Raspberry_Pi_1.GPIO8, Raspberry_Pi_Sense_Hat1.GIPO8
  N23: Raspberry_Pi_1.GPIO25, Raspberry_Pi_Sense_Hat1.GIPO25
  N24: Raspberry_Pi_1.GPIO24, Raspberry_Pi_Sense_Hat1.GIPO24
  N25: Raspberry_Pi_1.GPIO23, Raspberry_Pi_Sense_Hat1.GIPO23
  N26: Raspberry_Pi_1.GPIO18, Raspberry_Pi_Sense_Hat1.GIPO18
  N27: Raspberry_Pi_1.GPIO15, Raspberry_Pi_Sense_Hat1.GIPO15
  N28: Raspberry_Pi_1.GPIO14, Raspberry_Pi_Sense_Hat1.GIPO14
  5V: Raspberry_Pi_1.5V, Raspberry_Pi_Sense_Hat1.5V
  N29: Part1.A0, Smoke_detector_(FC22).DO
  N30: Part1.D11_PWM, Air_quality_(SDS1).RX
  N31: Part1.D10_PWM, Air_quality_(SDS1).TX
  5V_2: Part1.5V, Air_quality_(SDS1).5v, Smoke_detector_(FC22).VCC
  GND_2: Part1.GND, Air_quality_(SDS1).GND, Smoke_detector_(FC22).GND

custom parts:
  SDS011 - dust sensor: The SDS 011 Sensor is a quite recent Air Quality Sensor developed by inovafit, a spin-off from the university of Jinan (in Shandong). With its size, it is probably one of the best sensor in terms of accuracy: While other sensors tend to focus on shrinking the sensor size, the SDS 011 has opted for a size tradeoff allowing it to use a larger fan. And the larger the fan, the better the quality.
  MQ-7 breakout: MQ-5 gas sensor
  Raspberry Pi Sense Hat: The Sense HAT is an add-on board for Raspberry Pi, made especially for the Astro Pi mission – it launched to the International Space Station in December 2015. The Sense HAT has an 8×8 RGB LED matrix, a five-button joystick and includes the following sensors: Gyroscope Accelerometer Magnetometer Temperature Barometric pressure Humidity
  USB A Plug: USB A Plug breadboard only for documetnation purposes.
